# Fritzing sketch ODMS_Sharp (saved by Fritzing 0.9.3b)

parts:
  J1 = Infrared Proximity Sensor
  Часть1 = Arduino Uno (Rev3)

nets:
  N1: J1.Vout, Часть1.A0
  GND: J1.GND, Часть1.GND
  VCC: J1.Vcc, Часть1.5V
